# Fritzing sketch arduino-extram (saved by Fritzing 0.9.6b)
breadboards: 1

parts:
  U1 = 74HC595 [package="DIP16 [THT]"]
  U2 = 74HC595 [package="DIP16 [THT]"]
  SRAM1 = HM3-2064-5
  Part1 = Arduino Uno (Rev3)

nets:
  N1: U1.Q1, SRAM1.pin_6
  N2: U1.Q2, SRAM1.pin_5
  N3: U1.Q3, SRAM1.pin_4
  N4: U1.Q4, SRAM1.pin_3
  N5: U1.Q5, SRAM1.pin_25
  N6: U1.Q6, U2.DS, SRAM1.pin_24
  N7: U1.Q7, SRAM1.pin_21
  GND: U1.GND, U1.OE, U2.GND, U2.OE, SRAM1.pin_14, SRAM1.pin_20, Part1.GND
  VCC: U1.MR, U1.VCC, U2.MR, U2.VCC, SRAM1.pin_26, SRAM1.pin_28, Part1.5V
  N8: U1.SH_CP, U1.ST_CP, U2.SH_CP, U2.ST_CP, Part1.A3
  N9: U1.DS, SRAM1.pin_8, Part1.A2
  N10: U1.Q0, SRAM1.pin_7
  N11: U2.Q1, SRAM1.pin_2
  N12: U2.Q0, SRAM1.pin_23
  N13: SRAM1.pin_9, Part1.A1
  N14: SRAM1.pin_10, Part1.A0
  N15: SRAM1.pin_11, Part1.D8
  N16: SRAM1.pin_12, Part1.D9_PWM
  N17: SRAM1.pin_13, Part1.D10_PWM/SS
  N18: SRAM1.pin_15, Part1.D11_PWM/MOSI
  N19: SRAM1.pin_16, Part1.D4
  N20: SRAM1.pin_17, Part1.D5_PWM
  N21: SRAM1.pin_18, Part1.D6_PWM
  N22: SRAM1.pin_19, Part1.D7
  N23: SRAM1.pin_22, Part1.D12/MISO
  N24: SRAM1.pin_27, Part1.D13/SCK

custom parts:
  HM3-2064-5: HM3-2064-5 SRAM 8192 x 8 Bit
